// Logisim project problem3.circ as structural Verilog
module main (
  input  en,
  input  [3:0] data,
  output [7:0] display
);

  problem3 problem3_1 (.en(en), .data(data), .display(display));
  _7_Segment_Display a (
    .g(display[1]), .f(display[2]), .a(display[7]), .b(display[6]), .e(display[3]), .d(display[4]),
    .c(display[5]), .dp(display[0]));
endmodule

// VHDL entity problem3, as the project stores it:
library ieee;
use ieee.std_logic_1164.all;

entity problem3 is
    port(
        en : in std_logic;
        data : in std_logic_vector(3 downto 0);
        display : out std_logic_vector(7 downto 0)
    );
end entity problem3;

architecture bhv of problem3 is
begin
    process(en, data)
    begin
        if en = '0' then
            display <= "00000000";
        else
            case data is
                when "0000" => display <= "11101110"; -- a
                when "0001" => display <= "00111110"; -- b
                when "0010" => display <= "00011010"; -- c
                when "0011" => display <= "01111010"; -- d
                when "0100" => display <= "10001110"; -- f
                when "0101" => display <= "11110110"; -- g
                when others => display <= "00000000";
            end case;
        end if;
    end process;
end architecture bhv;
