// Logisim project problem5.circ as structural Verilog
module main (
  input  [12:0] vt,
  input  en,
  output [7:0] display
);

  problem5 problem5_1 (.vt(vt), .en(en), .display(display));
  _7_Segment_Display u_7_segment_display_1 (
    .g(display[1]), .f(display[2]), .a(display[7]), .b(display[6]), .e(display[3]), .d(display[4]),
    .c(display[5]), .dp(display[0]));
endmodule

// VHDL entity problem5, as the project stores it:
library ieee;
use ieee.std_logic_1164.all;

entity problem5 is
    port(
        vt : in std_logic_vector(12 downto 0);
        en : in std_logic;
        display : out std_logic_vector(7 downto 0)
    );
end entity problem5;

architecture bhv of problem5 is
begin
    process(vt, en)
        variable sum : integer range 0 to 13;
    begin
        sum := 0;

        for i in 0 to 12 loop
            if vt(i) = '1' then
                sum := sum + 1;
            end if;
        end loop;

        if en = '0' then
            display <= "00000000";
        else
            case sum is
                when 0  => display <= "11111100"; -- 0
                when 1  => display <= "01100000"; -- 1
                when 2  => display <= "11011010"; -- 2
                when 3  => display <= "11110010"; -- 3
                when 4  => display <= "01100110"; -- 4
                when 5  => display <= "10110110"; -- 5
                when 6  => display <= "10111110"; -- 6
                when 7  => display <= "11100000"; -- 7
                when 8  => display <= "11111110"; -- 8
                when 9  => display <= "11110110"; -- 9
                when 10 => display <= "11101110"; -- A
                when 11 => display <= "00111110"; -- b
                when 12 => display <= "10011100"; -- C
                when 13 => display <= "01111010"; -- d
                when others => display <= "00000000";
            end case;
        end if;
    end process;
end architecture bhv;
