// Logisim project problem1.circ as structural Verilog
module main (
  input  a,
  input  b,
  input  c,
  input  d,
  output out_5,
  output out_6
);

  problem1 problem1_1 (.a(a), .b(b), .c(c), .d(d), .and_out(out_5), .or_out(out_6));
endmodule

// VHDL entity problem1, as the project stores it:
library ieee;
use ieee.std_logic_1164.all;

entity problem1 is
    port(
        a, b, c, d : in std_logic;
        and_out, or_out : out std_logic
    );
end entity problem1;

architecture bhv of problem1 is
begin
    and_out <= a and b and c and d;
    or_out <= a or b or c or d;
end architecture bhv;
